// Logisim project TESTE.circ as structural Verilog: 3 circuits, main circuit main
module main (
  input  in_1,
  input  in_2,
  input  in_3,
  input  [3:0] in_4,
  input  [3:0] in_5,
  output out_6,
  output out_7,
  output out_8
);

  ADD_1 add_1_1 (.in_1(in_1), .in_2(in_2), .in_3(in_3), .out_4(out_7), .out_5(out_6));
  ADD_4 add_4_1 (.in_2(in_4), .out_3(out_8), .in_1(in_5));  // open: out_4
endmodule

module ADD_1 (
  input  in_1,
  input  in_2,
  input  in_3,
  output out_4,
  output out_5
);

  wire and_1_out, and_2_out, and_3_out, and_4_out, and_5_out, and_6_out, and_7_out, not_1_out, not_2_out,
       not_3_out, not_4_out, not_5_out, not_6_out;

  not not_1 (not_1_out, in_1);
  not not_2 (not_2_out, in_2);
  not not_3 (not_3_out, in_1);
  not not_4 (not_4_out, in_3);
  not not_5 (not_5_out, in_2);
  not not_6 (not_6_out, in_3);
  and and_1 (and_1_out, in_2, in_3);
  and and_2 (and_2_out, in_1, in_3);
  and and_3 (and_3_out, in_1, in_2);
  and and_4 (and_4_out, not_1_out, not_2_out, in_3);
  and and_5 (and_5_out, not_3_out, in_2, not_4_out);
  and and_6 (and_6_out, in_1, not_5_out, not_6_out);
  and and_7 (and_7_out, in_1, in_2, in_3);
  or or_1 (out_5, and_1_out, and_2_out, and_3_out);
  ExactlyOne xor_1 (.out(out_4), .in0(and_4_out), .in1(and_5_out), .in2(and_6_out), .in3(and_7_out));
endmodule

module ADD_4 (
  input  [3:0] in_1,
  input  [3:0] in_2,
  output out_3,
  output [3:0] out_4
);

  wire add_1_2_out_5, add_1_3_out_5, add_1_4_out_5;

  // Probe on in_2
  ADD_1 add_1_1 (.in_1(in_2[3]), .in_2(in_1[3]), .in_3(add_1_2_out_5), .out_4(out_4[3]), .out_5(out_3));
  ADD_1 add_1_2 (.in_1(in_2[2]), .in_2(in_1[2]), .in_3(add_1_3_out_5), .out_4(out_4[2]), .out_5(add_1_2_out_5));
  // Probe on out_4
  ADD_1 add_1_3 (.in_1(in_2[1]), .in_2(in_1[1]), .in_3(add_1_4_out_5), .out_4(out_4[1]), .out_5(add_1_3_out_5));
  ADD_1 add_1_4 (.in_1(in_2[0]), .in_2(in_1[0]), .in_3(1'b0), .out_4(out_4[0]), .out_5(add_1_4_out_5));
  // Probe on in_1
endmodule
